# Fritzing sketch 2wd_car (saved by Fritzing 0.9.3b)

parts:
  Part1 = Arduino Uno (Rev3) - ICSP
  S1 = H-Bridge with L298N
  M1 = DC Motor
  M2 = DC Motor
  VCC1 = 4 x AAA Battery Mount
  J1 = Basic Servo
  hc-sr1 = hc-sr04

nets:
  N1: Part1.ICSP_MOSI, Part1.D11_PWM/MOSI, hc-sr1.Trig
  N2: Part1.D8, S1.IN2
  N3: Part1.D9_PWM, J1.pulse
  N4: Part1.D12/MISO, hc-sr1.Echo
  GND: Part1.GND, S1.GND, VCC1.-, J1.gnd, hc-sr1.GND
  N5: Part1.D3_PWM, S1.IN3
  N6: Part1.D4, S1.IN4
  N7: Part1.D5_PWM, S1.ENB
  N8: Part1.D6_PWM, S1.ENA
  N9: Part1.D7, S1.IN1
  5V: Part1.5V, S1.5V, hc-sr1.VCC
  12V: S1.12V, VCC1.+, J1.vcc
  N10: S1.M1-01, M2.pin_2
  N11: S1.M1-02, M2.pin_1
  N12: S1.M2-01, M1.pin_2
  N13: S1.M2-02, M1.pin_1

custom parts:
  H-Bridge with L298N: h-bridge
